# Fritzing sketch TempSensor (saved by Fritzing 0.5.2b)
breadboards: 1

parts:
  Arduino1 = Arduino
  Q1 = NPN-Transistor [package="TO92 [THT]"]

nets:
  N1: Arduino1.aref, Arduino1.3V3, Q1.E
  N2: Arduino1.GND, Q1.C
  N3: Arduino1.A0, Q1.B
