# Fritzing sketch IR Sensor (saved by Fritzing 0.5.2b)
breadboards: 2

parts:
  VCC1 = obsolete Battery
  VCC2 = obsolete Battery
  LED1 = Red LED - 5mm [package="5 mm [THT]"]
  Q1 = PNP-Transistor [package="TO92 [THT]"]
  R1 = Resistor [resistance=220 package=THT]
  Arduino1 = Arduino
  Q2 = PNP-Transistor [package="TO92 [THT]"]

nets:
  N1: VCC1.-, Q1.B
  N2: VCC1.+, VCC2.-
  N3: VCC2.+, LED1.anode, Q1.C
  N4: LED1.cathode, R1.Pin_0
  N5: Q1.E, R1.Pin_1
  N6: Arduino1.D2, Q2.E
  N7: Arduino1.+5V, Q2.C
  N8: Arduino1.GND, Q2.B
